# Fritzing sketch light_sensor (saved by Fritzing 0.9.3b)
breadboards: 1

parts:
  Part1 = Arduino Uno (Rev3)
  R1 = Resistor [tolerance=±5% resistance=220 package=THT]
  R3 = Photocell (LDR) [package=THT]
  LED1 = smd LED [color="Red (633nm)" package="1206 [SMD]"]
  R4 = Resistor [tolerance=±5% resistance=10k package=THT]

nets:
  N1: Part1.A0, R3.pin_0, R4.Pin_1
  N2: Part1.GND, R3.pin_1, LED1.cathode
  N3: Part1.5V, R1.Pin_1, R4.Pin_0
  N4: R1.Pin_0, LED1.anode
