# Fritzing sketch ultrasonic_sensor (saved by Fritzing 0.9.3b)
breadboards: 1

parts:
  Part1 = Arduino Uno (Rev3)
  R1 = Resistor [tolerance=±5% resistance=220 package=THT]
  LED1 = smd LED [color="Red (633nm)" package="1206 [SMD]"]
  hc-sr1 = hc-sr04

nets:
  N1: Part1.D10_PWM/SS, hc-sr1.Trig
  N2: Part1.D11_PWM/MOSI, hc-sr1.Echo
  N3: Part1.D12/MISO, LED1.anode
  5V: Part1.5V, hc-sr1.VCC
  GND: Part1.GND, R1.Pin_0, hc-sr1.GND
  N4: R1.Pin_1, LED1.cathode
